// Digital circuit BancoReg.dig as structural Verilog
module BancoReg (
  input  [4:0] RegRd1,
  input  [4:0] RegRd2,
  input  [4:0] RegWr,
  input  [31:0] WrData,
  input  Write,
  input  rst,
  input  clk,
  input  [4:0] RbAdd,
  output [31:0] RdData2,
  output [31:0] RdData1,
  output [31:0] Rb
);

  BancoReg #(.applicationType("IVERILOG")) u_BancoReg (
    .RegRd1(RegRd1), .RegRd2(RegRd2), .RegWr(RegWr), .WrData(WrData), .Write(Write), .rst(rst), .clk(clk),
    .RbAdd(RbAdd), .RdData1(RdData1), .RdData2(RdData2), .Rb(Rb));
endmodule

/* Test case ULA:
	clk 	rst 	RegRd1     RegRd2 	RegWr 	WrData 	Write 	RdData1 	RdData2
	c    	0     	0        0      	0      	0     	0     	0       	0
	c    	1     	0        0      	0      	0     	0     	0       	0

loop(n,32)
     	c    	1     (n)     	(n)      	0     	0  	0   	(n)       	(n)
end loop
	c    	1     (0)    	(0)      	(0)     1   	1   	x       	x
loop(n,32)
	c    	1     (n)    	(n)      	(n)     (31-n)   1   	x       	x
end loop
loop(n,31)
	c    	1     (n)    	(n)      	(n)     0  	0  	(31-n)       	(31-n)
end loop
*/

/* Code of BancoReg:
module BancoReg(
input [4:0] RegRd1,
input [4:0] RegRd2,
input [4:0] RegWr,
input [31:0] WrData,
input Write,
input rst,
input clk,
input [4:0] RbAdd,
output [31:0] RdData1,
output [31:0] RdData2,
output [31:0] Rb
);
	reg [31:0] banco [0:31];
		
		assign RdData1 = banco[RegRd1];
		assign RdData2 = banco[RegRd2];
		assign Rb = banco[RbAdd];
		
		always @ (posedge clk or negedge rst) 
			begin
				if(rst == 0)
					begin
						banco[0] <= 0;
						banco[1] <= 1;
						banco[2] <= 2;
						banco[3] <= 3;
						banco[4] <= 4;
						banco[5] <= 5;
						banco[6] <= 6;
						banco[7] <= 7;
						banco[8] <= 8;
						banco[9] <= 9;
						banco[10] <= 10;
						banco[11] <= 11;
						banco[12] <= 12;
						banco[13] <= 13;
						banco[14] <= 14;
						banco[15] <= 15;
						banco[16] <= 16;
						banco[17] <= 17;
						banco[18] <= 18;
						banco[19] <= 19;
						banco[20] <= 20;
						banco[21] <= 21;
						banco[22] <= 22;
						banco[23] <= 23;
						banco[24] <= 24;
						banco[25] <= 25;
						banco[26] <= 26;
						banco[27] <= 27;
						banco[28] <= 28;
						banco[29] <= 29;
						banco[30] <= 30;
						banco[31] <= 31;
					end
				else if (Write == 1) begin
					banco[RegWr] <= WrData;
				end
			end
endmodule
*/
