// Digital circuit ULA.dig as structural Verilog
module ULA (
  input  [31:0] A,
  input  [31:0] B,
  input  [3:0] Op,
  output [31:0] Y,
  output Z
);

  ULA #(.applicationType("IVERILOG")) u_ULA (
    .operand1(A[0]), .operand2(B[0]), .ALU_control_vector(Op[0]), .zero(Z), .ALU_result(Y[0]));
  // Pins of 1 and 32 bits meet at Y
  // Pins of 1 and 32 bits meet at A
  // Pins of 1 and 32 bits meet at B
  // Pins of 1 and 4 bits meet at Op
endmodule

/* Test case ULA:
A B Op Z Y
 loop(i,5)
   let a = random(1<<32);
   let b = random(1<<32);
   (a) (b) 0 (ite((a & a)=0,1,0)) (a & b)
   (a) (b) 1 (ite((a | a)=0,1,0)) (a | b)
   (a) (b) 2 (ite((a + a)=0,1,0)) (a + b)
   (a) (b) 6 (ite((a - b)=0,1,0)) (a - b)
   (a) (a) 6 (ite((a - a)=0,1,0)) (a - a)
   (a) (b) 7 (ite((a < b)=0,1,0)) (a < b)
   
  end loop
*/

/* Code of ULA:
module ULA(input operand1, operand2, ALU_control_vector, output zero, ALU_result);
always @(ALU_control_vector)
begin
  case(ALU_control_vector)
    4'b0000: ALU_result = operand1 & operand2;
    default: zero = 0;
end
endmodule
*/
