// Digital circuit processador.dig as structural Verilog
module processador (
  input  Clk,
  input  nRst,
  input  [4:0] RbAdd,
  input  nHalt
);

  wire and_2_out, Clk_t, not_1_out, u_control_alusrc, u_control_branch, u_control_memtoreg,
       u_control_memwrite, u_control_regdst, u_control_regwrite, u_ULA_zero;
  wire [1:0] u_control_aluop;
  wire [3:0] ULA_Op;
  wire [4:0] Rd, RegWr, Rs, Rt;
  wire [5:0] ROM_d;
  wire [7:0] u_RegistradorPC_y_2;
  wire [10:6] ROM_d_2;
  wire [31:0] blockramdualport_1_d, Rb, u_BancoReg_rddata2, u_ExtensorSinal_y, u_Mux2x1_32bits_y,
       u_RegistradorPC_y, u_Soma4_y, u_somaPcDesvio_enderecodesvio, ULA_R1, ULA_R2, ULA_Result, WrData;
  wire [31:26] ROM_d_3;

  // Probe RbAdd on RbAdd
  // Probe Rb on Rb
  // Probe Rs on Rs
  // Probe Rt on Rt
  // Probe Rd on Rd
  // Probe RegWr on RegWr
  // Probe ULA_2 on ULA_R2
  // Probe Ula_1 on ULA_R1
  // Probe ResultULA on ULA_Result
  // Probe WrData on WrData
  // Probe ULA_op on ULA_Op
  // ScopeTrigger #(.maxStepCount(100)) scopetrigger_1: pin names not known; wires that end beside it: Clk_t
  Seven_Seg_Hex seven_seg_hex_1 (.d({3'b000, RbAdd[4]}), .dp(1'b0));
  Seven_Seg_Hex seven_seg_hex_2 (.d(RbAdd[3:0]), .dp(1'b0));
  // Probe Endereço on u_Mux2x1_32bits_y
  RegistradorPC #(.applicationType("IVERILOG")) u_RegistradorPC (
    .A(u_Mux2x1_32bits_y), .Clk(Clk_t), .Rst(nRst),
    .Y({u_RegistradorPC_y[31:10], u_RegistradorPC_y_2, u_RegistradorPC_y[1:0]}));
  and and_1 (Clk_t, Clk, nHalt);
  Seven_Seg_Hex seven_seg_hex_3 (.d(Rb[31:28]), .dp(1'b0));
  Soma4 #(.applicationType("IVERILOG")) u_Soma4 (
    .A({u_RegistradorPC_y[31:10], u_RegistradorPC_y_2, u_RegistradorPC_y[1:0]}), .Y(u_Soma4_y));
  Seven_Seg_Hex seven_seg_hex_4 (.d(Rb[27:24]), .dp(1'b0));
  Mux2x1_32bits #(.applicationType("IVERILOG")) u_Mux2x1_32bits (
    .A(u_Soma4_y), .B(u_somaPcDesvio_enderecodesvio), .S(and_2_out), .Y(u_Mux2x1_32bits_y));
  ROM #(.bigEndian("true"), .AddrBits(8), .isProgramMemory("true"), .Bits(32)) ROM (
    .A(u_RegistradorPC_y_2), .sel(1'b1), .D({ROM_d_3, Rs, Rt, Rd, ROM_d_2, ROM_d}));
  Seven_Seg_Hex seven_seg_hex_5 (.d(Rb[23:20]), .dp(1'b0));
  and and_2 (and_2_out, u_ULA_zero, u_control_branch);
  // Probe Instrução on {ROM_d_3, Rs, Rt, Rd, ROM_d_2, ROM_d}
  control #(.applicationType("IVERILOG")) u_control (
    .instruction({ROM_d_3, Rs, Rt, Rd, ROM_d_2, ROM_d}), .RegDst(u_control_regdst),
    .MemtoReg(u_control_memtoreg), .ALUSrc(u_control_alusrc), .Branch(u_control_branch),
    .MemWrite(u_control_memwrite), .RegWrite(u_control_regwrite), .ALUOp(u_control_aluop));
  Seven_Seg_Hex seven_seg_hex_6 (.d(Rb[19:16]), .dp(1'b0));
  Seven_Seg_Hex seven_seg_hex_7 (.d(Rb[15:12]), .dp(1'b0));
  ExtensorSinal #(.applicationType("IVERILOG")) u_ExtensorSinal (.A({Rd, ROM_d_2, ROM_d}), .Y(u_ExtensorSinal_y));
  Seven_Seg_Hex seven_seg_hex_8 (.d(Rb[11:8]), .dp(1'b0));
  Seven_Seg_Hex seven_seg_hex_9 (.d(Rb[7:4]), .dp(1'b0));
  Seven_Seg_Hex seven_seg_hex_10 (.d(Rb[3:0]), .dp(1'b0));
  Mux2x1_5bits #(.applicationType("IVERILOG")) u_Mux2x1_5bits (.S(u_control_regdst), .A(Rt), .B(Rd), .Y(RegWr));
  BancoReg #(.applicationType("IVERILOG")) u_BancoReg (
    .RegRd1(Rs), .RegRd2(Rt), .RegWr(RegWr), .WrData(WrData), .Write(u_control_regwrite), .rst(nRst),
    .clk(Clk_t), .RbAdd(RbAdd), .RdData1(ULA_R1), .RdData2(u_BancoReg_rddata2), .Rb(Rb));
  somaPcDesvio #(.applicationType("IVERILOG")) u_somaPcDesvio (
    .endereco(u_Soma4_y), .desvio(u_ExtensorSinal_y), .enderecoDesvio(u_somaPcDesvio_enderecodesvio));
  ALU_control #(.applicationType("IVERILOG")) u_ALU_control (
    .ALUOp(u_control_aluop), .funct(ROM_d), .ALU_control_vector(ULA_Op));
  Mux2x1_32bits #(.applicationType("IVERILOG")) u_Mux2x1_32bits_2 (
    .S(u_control_alusrc), .A(u_BancoReg_rddata2), .B(u_ExtensorSinal_y), .Y(ULA_R2));
  ULA #(.applicationType("IVERILOG")) u_ULA (
    .operand1(ULA_R1), .operand2(ULA_R2), .ALU_control_vector(ULA_Op), .zero(u_ULA_zero),
    .ALU_result(ULA_Result));
  not not_1 (not_1_out, Clk_t);
  BlockRAMDualPort #(.AddrBits(8), .isProgramMemory("true"), .Bits(32)) blockramdualport_1 (
    .A(ULA_Result[7:0]), .Din(u_BancoReg_rddata2), .str(u_control_memwrite), .C(not_1_out),
    .D(blockramdualport_1_d));
  Mux2x1_32bits #(.applicationType("IVERILOG")) u_Mux2x1_32bits_3 (
    .S(u_control_memtoreg), .A(ULA_Result), .B(blockramdualport_1_d), .Y(WrData));

  // Notes on the sheet:
  //   contents of ROM (hex, n*v repeats v):
  //   20f80100,22f00200,24e8e501,25e02200,1b8c,1eac,f9ff0010
endmodule

/* Code of RegistradorPC:
module RegistradorPC(input [31:0]A,input Clk,input Rst, output reg [31:0]Y);
     always @ (posedge Clk or negedge Rst)
	begin
            if (Rst == 0)
                Y <= 3'b0;
    	    else
                Y <= A;
        end
endmodule
*/

/* Code of Soma4:
module Soma4(input wire [31:0]A, output wire [31:0]Y);
    assign Y = A + 32'd4;
endmodule
*/

/* Code of Mux2x1_32bits:
module Mux2x1_32bits(
        input [31: 0] A, B,
	input S,
	output [31:0] Y
);
   assign Y = (S==0 ? A: B);
endmodule
*/

/* Code of control:
module control(input [31:0] instruction,output RegDst, MemtoReg, ALUSrc, Branch,  MemWrite, RegWrite,output [1:0] ALUOp);  





wire [5:0] Op = instruction[31:26];

reg [7:0] Control;

assign RegDst = Control[7];
assign RegWrite = Control[6];
assign ALUSrc = Control[5];
assign MemWrite = Control[4];
assign MemtoReg = Control[3];
assign Branch = Control[2];
assign ALUOp = Control[1:0];

initial
    Control = 7'd0;

always @(*)
    casex(Op)
        32'd0 : Control = 8'b11000010; // R-TYPE

        32'd35 : Control = 8'b01101000; // LW

        32'd43 : Control = 8'bx011x000; // SW

        32'd4 : Control = 8'bx000x101; // BEQ

        default : Control = 8'b00000000; // NOP  
    endcase

endmodule
*/

/* Code of ExtensorSinal:
module ExtensorSinal(input [15:0]A, output [31:0]Y);
   assign Y = (A[15] == 1 ? {31'b1} : {31'b0});
endmodule
*/

/* Code of Mux2x1_5bits:
module Mux2x1_5bits(
input S,
input [4:0]A,
input [4:0]B,
output [4:0]Y);
   assign Y = (S == 0 ? A : B);
endmodule
*/

/* Code of BancoReg:
module BancoReg(
input [4:0] RegRd1,
input [4:0] RegRd2,
input [4:0] RegWr,
input [31:0] WrData,
input Write,
input rst,
input clk,
input [4:0] RbAdd,
output [31:0] RdData1,
output [31:0] RdData2,
output [31:0] Rb
);
    reg [31:0] banco [0:31];

        assign RdData1 = banco[RegRd1];
        assign RdData2 = banco[RegRd2];
        assign Rb = banco[RbAdd];

        always @ (posedge clk or negedge rst) 
            begin
                if(rst == 0)
                    begin
                        banco[0] <= 0;
                        banco[1] <= 1;
                        banco[2] <= 2;
                        banco[3] <= 3;
                        banco[4] <= 4;
                        banco[5] <= 5;
                        banco[6] <= 6;
                        banco[7] <= 7;
                        banco[8] <= 8;
                        banco[9] <= 9;
                        banco[10] <= 10;
                        banco[11] <= 11;
                        banco[12] <= 12;
                        banco[13] <= 13;
                        banco[14] <= 14;
                        banco[15] <= 15;
                        banco[16] <= 16;
                        banco[17] <= 17;
                        banco[18] <= 18;
                        banco[19] <= 19;
                        banco[20] <= 20;
                        banco[21] <= 21;
                        banco[22] <= 22;
                        banco[23] <= 23;
                        banco[24] <= 24;
                        banco[25] <= 25;
                        banco[26] <= 26;
                        banco[27] <= 27;
                        banco[28] <= 28;
                        banco[29] <= 29;
                        banco[30] <= 30;
                        banco[31] <= 31;
                    end
                else if (Write == 1) begin
                    banco[RegWr] <= WrData;
                end
            end
endmodule
*/

/* Code of somaPcDesvio:
module somaPcDesvio (
input [31:0]endereco,
input [31:0]desvio,
output reg [31:0]enderecoDesvio
);
	always @(*)begin
		enderecoDesvio={(endereco + desvio), 2'b0};
	end
endmodule
*/

/* Code of ALU_control:
module ALU_control(ALU_control_vector, ALUOp, funct);

output reg [3:0] ALU_control_vector;
input [1:0] ALUOp;
input [5:0] funct;

initial
    ALU_control_vector = 4'b0000;

always @(*)
begin
    case(ALUOp[1])
        1'b0 :  case(ALUOp[0])
                1'b0 : ALU_control_vector = 4'b0010; // ADD for LW, SW

                1'b1 : ALU_control_vector = 4'b0110; // SUB for BEQ
            endcase

        1'b1 :  case(funct[3:0])
                4'b0000 : ALU_control_vector = 4'b0010; // ADD

                4'b0100 : ALU_control_vector = 4'b0000; // AND

                4'b0101 : ALU_control_vector = 4'b0001; // OR

                4'b0010 : ALU_control_vector = 4'b0110; // SUB

                4'b1010 : ALU_control_vector = 4'b0111; // SLT

                default : ALU_control_vector = 4'b0010; // ADD (doesn't matter)
            endcase
    endcase
end

endmodule
*/

/* Code of Mux2x1_32bits:
module Mux2x1_32bits(
	input S,
        input [31: 0] A, B,
	output [31:0] Y
);
   assign Y = (S==0 ? A: B);
endmodule
*/

/* Code of ULA:
module ULA(
	input [31:0] operand1, operand2,
	input [3:0] ALU_control_vector,
        output reg zero,
	output [31:0] ALU_result
);

	reg [31:0] ALU_result;

	always @(*) begin
           case (ALU_control_vector)
              0: ALU_result = operand1 & operand2;
              1: ALU_result = operand1 | operand2;
              2: ALU_result = operand1 + operand2;
              6: ALU_result = operand1 - operand2;
	      7: ALU_result = operand1 < operand2;
              12: ALU_result = ~(operand1 | operand2);
	      default: ALU_result = 32'd0;
	   endcase
	   if(ALU_result == 32'd0)begin
           	zero = 1'b1;
           end else begin
	   	zero = 1'b0;
           end
        end

endmodule
*/
