// Digital circuit somaPcDesvio.dig as structural Verilog
module somaPcDesvio (
  input  [31:0] endereco,
  input  [31:0] desvio,
  output [31:0] enderecoDesvio
);

  somaPcDesvio #(.applicationType("IVERILOG")) u_somaPcDesvio (
    .endereco(endereco), .desvio(desvio), .enderecoDesvio(enderecoDesvio));
endmodule

/* Test case somaPcDesvio:
endereco desvio enderecoDesvio
0       10	    40
100     (-5)          80
56	20	    136
32	(-8)	    0
*/

/* Code of somaPcDesvio:
module somaPcDesvio (
input [31:0]endereco,
input [31:0]desvio,
output reg [31:0]enderecoDesvio
);
	always @(*)begin
		enderecoDesvio={(endereco + desvio), 2'b0};
	end
endmodule
*/
