// Digital circuit template mux2x1_32.dig as structural Verilog
module template_mux2x1_32 (
  input  [31:0] A,
  input  [31:0] B,
  input  S,
  output [31:0] Y
);

  Mux2x1_32bits #(.applicationType("IVERILOG")) u_Mux2x1_32bits (.A(A), .B(B), .S(S), .Y(Y));
endmodule

/* Test case mux8:
A B S Y
 loop(i,10)
   let a = random(1<<8);
   let b = random(1<<8);
   (a) (b) 0 (a)
   (a) (b) 1 (b)
  end loop
*/

/* Code of Mux2x1_32bits:
module Mux2x1_32bits(
	input [31:0] A, B,
 	input S,
	output [31:0] Y
);
   assign Y = (S==0 ? A: B);
endmodule
*/
