// Digital circuit Prototipo_Processador.dig as structural Verilog
module Prototipo_Processador (
  input  Clk,
  input  nRst,
  input  [4:0] RbAdd,
  input  nHalt
);

  wire and_2_out, Clk_t, not_1_out, RegWr, u_control_alusrc, u_control_branch, u_control_memtoreg,
       u_control_memwrite, u_control_regdst, u_control_regwrite, u_ExtensorSinal_y, u_Mux2x1_32bits_y,
       u_Soma4_y, u_somaPcDesvio_enderecodesvio, u_ULA_zero, ULA_R1, ULA_R2, WrData;
  wire [1:0] u_control_aluop;
  wire [3:0] ULA_Op;
  wire [4:0] Rd, Rs, Rt;
  wire [5:0] ROM_d;
  wire [7:0] undriven;
  wire [10:6] ROM_d_2;
  wire [31:0] blockramdualport_1_d, Rb, u_BancoReg_rddata2, u_RegistradorPC_y, ULA_Result;
  wire [31:26] ROM_d_3;

  // Probe RbAdd on RbAdd
  // Probe Rb on Rb
  // Probe Rs on Rs
  // Probe Rt on Rt
  // Probe Rd on Rd
  // Probe RegWr on RegWr
  // Probe ULA_2 on ULA_R2
  // Probe Ula_1 on ULA_R1
  // Probe ResultULA on ULA_Result
  // Probe WrData on WrData
  // Probe ULA_op on ULA_Op
  // ScopeTrigger #(.maxStepCount(100)) scopetrigger_1: pin names not known; wires that end beside it: Clk_t
  Seven_Seg_Hex seven_seg_hex_1 (.d({3'b000, RbAdd[4]}), .dp(1'b0));
  Seven_Seg_Hex seven_seg_hex_2 (.d(RbAdd[3:0]), .dp(1'b0));
  // Probe Endereço on u_Mux2x1_32bits_y
  RegistradorPC #(.applicationType("IVERILOG")) u_RegistradorPC (
    .A(u_Mux2x1_32bits_y), .Clk(Clk_t), .Rst(nRst), .Y(u_RegistradorPC_y[0]));
  and and_1 (Clk_t, Clk, nHalt);
  Seven_Seg_Hex seven_seg_hex_3 (.d(Rb[31:28]), .dp(1'b0));
  Soma4 #(.applicationType("IVERILOG")) u_Soma4 (.A(u_RegistradorPC_y[0]), .Y(u_Soma4_y));
  Seven_Seg_Hex seven_seg_hex_4 (.d(Rb[27:24]), .dp(1'b0));
  Mux2x1_32bits #(.applicationType("IVERILOG")) u_Mux2x1_32bits (
    .A(u_Soma4_y), .B(u_somaPcDesvio_enderecodesvio), .S(and_2_out), .Y(u_Mux2x1_32bits_y));
  ROM #(.bigEndian("true"), .AddrBits(8), .isProgramMemory("true"), .Bits(32)) ROM (
    .A(undriven), .sel(1'b1), .D({ROM_d_3, Rs, Rt, Rd, ROM_d_2, ROM_d}));
  Seven_Seg_Hex seven_seg_hex_5 (.d(Rb[23:20]), .dp(1'b0));
  and and_2 (and_2_out, u_ULA_zero, u_control_branch);
  // Probe Instrução on {ROM_d_3, Rs, Rt, Rd, ROM_d_2, ROM_d}
  control #(.applicationType("IVERILOG")) u_control (
    .instruction({ROM_d_3, Rs, Rt, Rd, ROM_d_2, ROM_d}), .RegDst(u_control_regdst),
    .MemtoReg(u_control_memtoreg), .ALUSrc(u_control_alusrc), .Branch(u_control_branch),
    .MemWrite(u_control_memwrite), .RegWrite(u_control_regwrite), .ALUOp(u_control_aluop));
  Seven_Seg_Hex seven_seg_hex_6 (.d(Rb[19:16]), .dp(1'b0));
  Seven_Seg_Hex seven_seg_hex_7 (.d(Rb[15:12]), .dp(1'b0));
  ExtensorSinal #(.applicationType("IVERILOG")) u_ExtensorSinal (.A(ROM_d[0]), .Y(u_ExtensorSinal_y));
  Seven_Seg_Hex seven_seg_hex_8 (.d(Rb[11:8]), .dp(1'b0));
  Seven_Seg_Hex seven_seg_hex_9 (.d(Rb[7:4]), .dp(1'b0));
  Seven_Seg_Hex seven_seg_hex_10 (.d(Rb[3:0]), .dp(1'b0));
  mux2x1_5bits #(.applicationType("IVERILOG")) u_mux2x1_5bits (.S(u_control_regdst), .A(Rt[0]), .B(Rd[0]), .Y(RegWr));
  BancoReg #(.applicationType("IVERILOG")) u_BancoReg (
    .RegRd1(Rs[0]), .RegRd2(Rt[0]), .RegWr(RegWr), .WrData(WrData), .Write(u_control_regwrite), .rst(nRst),
    .clk(Clk_t), .RbAdd(RbAdd[0]), .RdData1(ULA_R1), .RdData2(u_BancoReg_rddata2[0]), .Rb(Rb[0]));
  somaPcDesvio #(.applicationType("IVERILOG")) u_somaPcDesvio (
    .endereco(u_Soma4_y), .desvio(u_ExtensorSinal_y), .enderecoDesvio(u_somaPcDesvio_enderecodesvio));
  ALU_control #(.applicationType("IVERILOG")) u_ALU_control (
    .ALUOp(u_control_aluop), .funct(ROM_d), .ALU_control_vector(ULA_Op));
  Mux2x1_32bits #(.applicationType("IVERILOG")) u_Mux2x1_32bits_2 (
    .S(u_control_alusrc), .A(u_BancoReg_rddata2[0]), .B(u_ExtensorSinal_y), .Y(ULA_R2));
  ULA #(.applicationType("IVERILOG")) u_ULA (
    .A(ULA_R1), .B(ULA_R2), .Op(ULA_Op[0]), .zero(u_ULA_zero), .Y(ULA_Result[0]));
  not not_1 (not_1_out, Clk_t);
  BlockRAMDualPort #(.AddrBits(8), .isProgramMemory("true"), .Bits(32)) blockramdualport_1 (
    .A(ULA_Result[7:0]), .Din(u_BancoReg_rddata2), .str(u_control_memwrite), .C(not_1_out),
    .D(blockramdualport_1_d));
  Mux2x1_32bits #(.applicationType("IVERILOG")) u_Mux2x1_32bits_3 (
    .S(u_control_memtoreg), .A(ULA_Result[0]), .B(blockramdualport_1_d[0]), .Y(WrData));
  // Pins of 1 and 16 bits meet at {Rd, ROM_d_2, ROM_d}
  // Pins of 1 and 5 bits meet at Rt
  // Pins of 1 and 5 bits meet at Rs
  // Pins of 1 and 5 bits meet at Rd
  // Pins of 1 and 32 bits meet at u_BancoReg_rddata2
  // Pins of 1 and 32 bits meet at blockramdualport_1_d
  // Pins of 1 and 32 bits meet at ULA_Result
  // Pins of 1 and 5 bits meet at RbAdd
  // Pins of 1 and 32 bits meet at {u_RegistradorPC_y[31:10], undriven, u_RegistradorPC_y[1:0]}
  // Pins of 1 and 4 bits meet at ULA_Op
  // Pins of 1 and 32 bits meet at Rb

  // Notes on the sheet:
  //   ROM loads TesteBeq.hex
endmodule

/* Code of RegistradorPC:
module RegistradorPC(input A, Clk, Rst, output Y);
endmodule
*/

/* Code of Soma4:
module Soma4(input A, output Y);
endmodule
*/

/* Code of Mux2x1_32bits:
module Mux2x1_32bits(input A, B, input S, output Y);
endmodule
*/

/* Code of control:
module control(input [31:0] instruction,output RegDst, MemtoReg, ALUSrc, Branch,  MemWrite, RegWrite,output [1:0] ALUOp);  





wire [5:0] Op = instruction[31:26];

reg [7:0] Control;

assign RegDst = Control[7];
assign RegWrite = Control[6];
assign ALUSrc = Control[5];
assign MemWrite = Control[4];
assign MemtoReg = Control[3];
assign Branch = Control[2];
assign ALUOp = Control[1:0];

initial
    Control = 7'd0;

always @(*)
    casex(Op)
        32'd0 : Control = 8'b11000010; // R-TYPE

        32'd35 : Control = 8'b01101000; // LW

        32'd43 : Control = 8'bx011x000; // SW

        32'd4 : Control = 8'bx000x101; // BEQ

        default : Control = 8'b00000000; // NOP  
    endcase

endmodule
*/

/* Code of ExtensorSinal:
module ExtensorSinal(input A, output Y);
endmodule
*/

/* Code of mux2x1_5bits:
module mux2x1_5bits (input S, A, B, output Y);
endmodule
*/

/* Code of BancoReg:
module BancoReg( input RegRd1, RegRd2, RegWr, WrData, Write, rst, clk, RbAdd, output RdData1, RdData2, Rb);

endmodule
*/

/* Code of somaPcDesvio:
module somaPcDesvio (input endereco, desvio, output enderecoDesvio);
endmodule
*/

/* Code of ALU_control:
module ALU_control(ALU_control_vector, ALUOp, funct);

output reg [3:0] ALU_control_vector;
input [1:0] ALUOp;
input [5:0] funct;

initial
    ALU_control_vector = 4'b0000;

always @(*)
begin
    case(ALUOp[1])
        1'b0 :  case(ALUOp[0])
                1'b0 : ALU_control_vector = 4'b0010; // ADD for LW, SW

                1'b1 : ALU_control_vector = 4'b0110; // SUB for BEQ
            endcase

        1'b1 :  case(funct[3:0])
                4'b0000 : ALU_control_vector = 4'b0010; // ADD

                4'b0100 : ALU_control_vector = 4'b0000; // AND

                4'b0101 : ALU_control_vector = 4'b0001; // OR

                4'b0010 : ALU_control_vector = 4'b0110; // SUB

                4'b1010 : ALU_control_vector = 4'b0111; // SLT

                default : ALU_control_vector = 4'b0010; // ADD (doesn't matter)
            endcase
    endcase
end

endmodule
*/

/* Code of Mux2x1_32bits:
module Mux2x1_32bits(input S, A, B,  output Y);
endmodule
*/

/* Code of ULA:
module ULA (input A, B, Op, output zero,  Y);
endmodule
*/

/* Code of Mux2x1_32bits:
module Mux2x1_32bits(input S, A, B, output Y);
endmodule
*/
