// Digital circuit template BancoReg.dig as structural Verilog
module template_BancoReg (
  input  [4:0] RegRd1,
  input  [4:0] RegRd2,
  input  [4:0] RegWr,
  input  [31:0] WrData,
  input  Write,
  input  rst,
  input  clk,
  input  RbAdd,
  output [31:0] RdData2,
  output [31:0] RdData1,
  output [31:0] Rb
);

  BancoReg #(.applicationType("IVERILOG")) u_BancoReg (
    .RegRd1(RegRd1[0]), .RegRd2(RegRd2[0]), .RegWr(RegWr[0]), .WrData(WrData[0]), .Write(Write), .rst(rst),
    .clk(clk), .RbAdd(RbAdd), .RdData1(RdData1[0]), .RdData2(RdData2[0]), .Rb(Rb[0]));
  // Pins of 1 and 32 bits meet at RdData2
  // Pins of 1 and 5 bits meet at RegRd1
  // Pins of 1 and 5 bits meet at RegRd2
  // Pins of 1 and 5 bits meet at RegWr
  // Pins of 1 and 32 bits meet at RdData1
  // Pins of 1 and 32 bits meet at WrData
  // Pins of 1 and 32 bits meet at Rb
endmodule

/* Test case ULA:
	clk 	rst 	RegRd1     RegRd2 	RegWr 	WrData 	Write 	RdData1 	RdData2
	c    	0     	0        0      	0      	0     	0     	0       	0
	c    	1     	0        0      	0      	0     	0     	0       	0

loop(n,32)
     	c    	1     (n)     	(n)      	0     	0  	0   	(n)       	(n)
end loop
	c    	1     (0)    	(0)      	(0)     1   	1   	x       	x
loop(n,32)
	c    	1     (n)    	(n)      	(n)     (31-n)   1   	x       	x
end loop
loop(n,31)
	c    	1     (n)    	(n)      	(n)     0  	0  	(31-n)       	(31-n)
end loop
*/

/* Code of BancoReg:
//assings de rbdatas e converter para 32 bits
module BancoReg( 
input [31:0]RegRd1,
input [31:0]RegRd2,
input RegWr,
input [31:0]WrData,
input Write,
input rst,
input clk,
input [4:0]RbAdd, //procurar onde põe
output [31:0]RdData1,
output [31:0]RdData2,
output Rb);

reg [31:0] dados [31:0];

     always @ (posedge clk or negedge rst)
	begin
            if (rst == 0)
		begin
			dados[0] <= 32'b0;
			dados[1] <= 32'b0;
	//... a posição 0 recebe 0, 1 recebe 1 e por assim vai
		end
    	    else
                Y <= A;
	    if (Write)
		dados[RegWr] <= WrData;
        end

endmodule
*/
