// Digital circuit template registradorPC.dig as structural Verilog
module template_registradorPC (
  input  [31:0] A,
  input  Clk,
  input  Rst,
  output [31:0] Y
);

  RegistradorPC #(.applicationType("IVERILOG")) u_RegistradorPC (.A(A), .Clk(Clk), .Rst(Rst), .Y(Y));
endmodule

/* Test case ULA:
Clk A Rst Y
 loop(i,10)
   let a = random(1<<16);
   c (a) 0 0
   c (a) 1 (a)
  end loop
*/

/* Code of RegistradorPC:
module RegistradorPC(input [31:0]A,input Clk,input Rst, output reg [31:0]Y);
     always @ (posedge Clk or negedge Rst)
	begin
            if (Rst == 0)
                Y <= 32'b0;
    	    else
                Y <= A;
        end
endmodule
*/
